# Fritzing sketch Node (saved by Fritzing 0.9.1b)
breadboards: 3

parts:
  T1 = LM34 Temperature Sensor [package="TO92 [THT]"]
  Part2 = Arduino Nano (Rev3.0)
  ENC28J1 = ENC28J60
  PIR1 = PIR sensor
  R1 = Photocell (LDR) [package=THT]
  R2 = Resistor [tolerance=±5% resistance=10k package=THT]
  RED = TRANSISTOR_NPN [package=to-92-ammo]
  LED1 = RGB LED (com. cathode, rbg) [package="5 mm [THT]"]
  U1 = Voltage Regulator [package=to220-adj]
  RED_2 = Resistor [tolerance=±5% resistance=3.9k package="1206 [SMD]"]
  LED2 = RGB LED (com. cathode, rbg) [package="5 mm [THT]"]
  LED4 = RGB LED (com. cathode, rbg) [package="5 mm [THT]"]
  GREEN = TRANSISTOR_NPN [package=to-92-ammo]
  BLUE = TRANSISTOR_NPN [package=to-92-ammo]
  GREE = Resistor [tolerance=±5% resistance=3.9k package="1206 [SMD]"]
  R9 = Resistor [tolerance=±5% resistance=270 package="1206 [SMD]"]
  R10 = Resistor [tolerance=±5% resistance=270 package="1206 [SMD]"]
  R16 = Resistor [tolerance=±5% resistance=270 package="1206 [SMD]"]
  LED5 = RGB LED (com. cathode, rbg) [package="5 mm [THT]"]
  BLUE_2 = Resistor [tolerance=±5% resistance=3.9k package="1206 [SMD]"]
  AlarmRedLED = smd LED [color="Red (633nm)" package="0805 [SMD]"]
  R17 = Resistor [tolerance=±5% resistance=1k package="1206 [SMD]"]
  R18 = Resistor [tolerance=±5% resistance=1k package="1206 [SMD]"]

nets:
  5V: T1.+Vs, Part2.5V, PIR1.VDD, R1.pin_1
  N1: T1.Vout, Part2.A0
  GND: T1.GND, Part2.GND, ENC28J1.GND, PIR1.GND, R2.Pin_1, LED1.common_cathode, LED2.common_cathode, LED4.common_cathode, LED5.common_cathode, R17.Pin_0
  N2: Part2.D2, PIR1.SIG
  N3: Part2.D3, GREE.Pin_1
  N4: Part2.D4, RED_2.Pin_1
  N5: Part2.D5, BLUE_2.Pin_1
  N6: Part2.D10, ENC28J1.CS
  N7: Part2.D11/MOSI, ENC28J1.SI
  N8: Part2.D12/MISO, ENC28J1.SO
  N9: Part2.A2, R17.Pin_1, R18.Pin_0
  N10: Part2.A1, R1.pin_0, R2.Pin_0
  3V3: Part2.3V3, ENC28J1.VCC
  N11: Part2.D13/SCK, ENC28J1.SCK, ENC28J1.RST
  N12: RED.E, R10.Pin_0
  N13: RED.B, RED_2.Pin_0
  N14: RED.C, U1.OUT, GREEN.C, BLUE.C
  N15: LED1.red_anode, LED2.red_anode, LED4.red_anode, R10.Pin_1, LED5.red_anode
  N16: LED1.blue_anode, LED2.blue_anode, LED4.blue_anode, R16.Pin_1, LED5.blue_anode
  N17: LED1.green_anode, LED2.green_anode, LED4.green_anode, R9.Pin_1, LED5.green_anode
  N18: GREEN.E, R16.Pin_0
  N19: GREEN.B, GREE.Pin_0
  N20: BLUE.E, R9.Pin_0
  N21: BLUE.B, BLUE_2.Pin_0
  N22: AlarmRedLED.cathode, R18.Pin_1

notes:
  5V Rail
  3.3V Rail
  Power from Smoke Alarm (9.4V)

custom parts:
  ENC28J60: Ethernet Module ENC28J60

// code stored in the sketch: Node.ino
/*
  UDPSendReceive.pde:
 This sketch receives UDP message strings, prints them to the serial port
 and sends an "acknowledge" string back to the sender
 
 A Processing sketch is included at the end of file that can be used to send 
 and received messages for testing with a computer.
 
 created 21 Aug 2010
 by Michael Margolis
 
 This code is in the public domain.
 */


#include <SPI.h>         // needed for Arduino versions later than 0018
#include <Ethernet.h>
#include <EthernetUdp.h>         // UDP library from: bjoern@cs.stanford.edu 12/30/2008
#include <avr/pgmspace.h>
#include "ChipTemp.h"


// Enter a MAC address and IP address for your controller below.
// The IP address will be dependent on your local network:
byte mac[] = { 0xDE, 0xAD, 0xBE, 0xEF, 0xFE, 0xED };
IPAddress ip(192, 168, 1, 177);     // Arduino IP address
IPAddress server(192, 168, 1, 39);  // Server IP address
unsigned int localPort = 8888;      // local port to listen on

int temp_pin = 0;        // the analog pin for LM34 temp sensor - Cannot use pin 0 as it is used for something by DRobotics LCD shield
float sensor_reading = 0.0;        // variable to store the value coming from the sensor
float vref = 1.04;        // variable to store the voltage reference used (check for validity with a DMM)
float fahrenheit = 0.0;        // variable to store the actual temperature
float centigrade = 0.0;
boolean debug = true;
int interval = 1000;


// buffers for receiving and sending data
char packetBuffer[UDP_TX_PACKET_MAX_SIZE]; //buffer to hold incoming packet,
char  ReplyBuffer[] = "acknowledged";       // a string to send back

// An EthernetUDP instance to let us send and receive packets over UDP
EthernetUDP Udp;
ChipTemp chipTemp;

void setup() {
  // start the Ethernet and UDP:
    pinMode( temp_pin, INPUT );        // set LM34 temp sensor pin as an input
 analogReference(INTERNAL);        // set the analog reference to the 1.1V internal reference
  Ethernet.begin(mac,ip);
  Udp.begin(localPort);

  Serial.begin(9600);
}

void loop() {
  receivePacket();
  String dataString;
  dataString += extTemp(); // Load external temperature into data string
  dataString += intTemp(); // Load internal temperature into data string
  char message[dataString.length()]; 
  dataString.toCharArray(message,dataString.length()); // convert string to char array
  sendPacket(message);
  delay(interval);
}

void sendPacket(char message[]) {
  Udp.beginPacket(server, localPort);
  Udp.write(message);
  Udp.endPacket();
}

void receivePacket() {
  int packetSize = Udp.parsePacket();
  if(packetSize)
  {
    Serial.print("Received packet of size ");
    Serial.println(packetSize);
    Serial.print("From ");
    if(debug) {
      IPAddress remote = Udp.remoteIP();
      for (int i =0; i < 4; i++)
      {
        Serial.print(remote[i], DEC);
        if (i < 3)
        {
          Serial.print(".");
        }
      }
      Serial.print(", port ");
      Serial.println(Udp.remotePort());
    }

    // read the packet into packetBufffer
    Udp.read(packetBuffer,UDP_TX_PACKET_MAX_SIZE);
    if(debug) {
      Serial.println("Contents:");
      Serial.println(packetBuffer);
    }
    testString(packetBuffer, (packetSize-2));
  }
}

void testString(char message[], int strLength) {
  int i,j,start;
  start = 0;
  for (i=0;i<=strLength;i++) 
    { //check entire string 
    if (message[i]==',') {//if comma found 
      /*for (j=0;j=i-1;j++)//for the beginning to the current position - 1 for the comma symbol 
      {
        temp[j]=message[j];//transfer the chars to temp string 
      }
      Serial.println(temp);
      for(j=i+1;j==strLength;j++)//the remaining after comma symbol
      {
        temp[j]=message[j];//transfer the remain chars
      }
      Serial.println(temp);*/
      for(j=start;j<i;j++) {
        Serial.print(message[j]);
        
      }
      Serial.println(); 
                Serial.println(); 
      start = i+1;
      //Serial.println("Found Comma!");
      //c1 = i;
      /*if(c1 == NULL) {
        c1 = i;
      } else {
         c2 = i;
      }*/
    } 
  }
          Serial.println(); 
  Serial.println(message[strLength]);
  //Serial.println(c1);
  //Serial.println(c2);
}

String extTemp() {
  String temp;
   //sensor_reading = analogRead(sensor_pin);         // stores the digitized (0 - 1023) analog reading from the LM34
   fahrenheit = (100.0 * analogRead(temp_pin) * vref)/1023;   // calculates the actual fahrenheit temperature
   centigrade = (((5.0/9.0))*(fahrenheit-32.0)); //conversion to degrees C
   temp += centigrade; temp += ',';
   temp += fahrenheit; temp += ',';
   if(debug) {
     Serial.print (centigrade); Serial.print("C "); 
     Serial.print(fahrenheit); Serial.print("F ");
   }
   return temp;
}

String intTemp() {
  String temp;
  temp += chipTemp.celsius(); temp += ',';
  temp += chipTemp.fahrenheit(); temp += ',';
  if(debug) {
    Serial.print (chipTemp.celsius()); Serial.print("C "); 
    Serial.print(chipTemp.fahrenheit()); Serial.println("F "); 
  }
  return temp;
}

// code stored in the sketch: UDPSend.ino
/*
  UDPSendReceive.pde:
 This sketch receives UDP message strings, prints them to the serial port
 and sends an "acknowledge" string back to the sender
 
 A Processing sketch is included at the end of file that can be used to send 
 and received messages for testing with a computer.
 
 created 21 Aug 2010
 by Michael Margolis
 
 This code is in the public domain.
 */


#include <SPI.h>         // needed for Arduino versions later than 0018
#include <Ethernet.h>
#include <EthernetUdp.h>         // UDP library from: bjoern@cs.stanford.edu 12/30/2008
#include <avr/pgmspace.h>
#include "ChipTemp.h"


// Enter a MAC address and IP address for your controller below.
// The IP address will be dependent on your local network:
byte mac[] = { 0xDE, 0xAD, 0xBE, 0xEF, 0xFE, 0xED };
IPAddress ip(192, 168, 1, 177);     // Arduino IP address
IPAddress server(192, 168, 1, 39);  // Server IP address
unsigned int localPort = 8888;      // local port to listen on

int temp_pin = 0;        // the analog pin for LM34 temp sensor - Cannot use pin 0 as it is used for something by DRobotics LCD shield
float sensor_reading = 0.0;        // variable to store the value coming from the sensor
float vref = 1.04;        // variable to store the voltage reference used (check for validity with a DMM)
float fahrenheit = 0.0;        // variable to store the actual temperature
float centigrade = 0.0;
boolean debug = true;
int interval = 1000;


// buffers for receiving and sending data
char packetBuffer[UDP_TX_PACKET_MAX_SIZE]; //buffer to hold incoming packet,
char  ReplyBuffer[] = "acknowledged";       // a string to send back

// An EthernetUDP instance to let us send and receive packets over UDP
EthernetUDP Udp;
ChipTemp chipTemp;

void setup() {
  // start the Ethernet and UDP:
    pinMode( temp_pin, INPUT );        // set LM34 temp sensor pin as an input
 analogReference(INTERNAL);        // set the analog reference to the 1.1V internal reference
  Ethernet.begin(mac,ip);
  Udp.begin(localPort);

  Serial.begin(9600);
}

void loop() {
  receivePacket();
  String dataString;
  dataString += extTemp(); // Load external temperature into data string
  dataString += intTemp(); // Load internal temperature into data string
  char message[dataString.length()]; 
  dataString.toCharArray(message,dataString.length()); // convert string to char array
  sendPacket(message);
  delay(interval);
}

void sendPacket(char message[]) {
  Udp.beginPacket(server, localPort);
  Udp.write(message);
  Udp.endPacket();
}

void receivePacket() {
  int packetSize = Udp.parsePacket();
  if(packetSize)
  {
    Serial.print("Received packet of size ");
    Serial.println(packetSize);
    Serial.print("From ");
    if(debug) {
      IPAddress remote = Udp.remoteIP();
      for (int i =0; i < 4; i++)
      {
        Serial.print(remote[i], DEC);
        if (i < 3)
        {
          Serial.print(".");
        }
      }
      Serial.print(", port ");
      Serial.println(Udp.remotePort());
    }

    // read the packet into packetBufffer
    Udp.read(packetBuffer,UDP_TX_PACKET_MAX_SIZE);
    if(debug) {
      Serial.println("Contents:");
      Serial.println(packetBuffer);
    }
    testString(packetBuffer, (packetSize-2));
  }
}

void testString(char message[], int strLength) {
  int i,j,start;
  start = 0;
  for (i=0;i<=strLength;i++) 
    { //check entire string 
    if (message[i]==',') {//if comma found 
      /*for (j=0;j=i-1;j++)//for the beginning to the current position - 1 for the comma symbol 
      {
        temp[j]=message[j];//transfer the chars to temp string 
      }
      Serial.println(temp);
      for(j=i+1;j==strLength;j++)//the remaining after comma symbol
      {
        temp[j]=message[j];//transfer the remain chars
      }
      Serial.println(temp);*/
      for(j=start;j<i;j++) {
        Serial.print(message[j]);
        
      }
      Serial.println(); 
                Serial.println(); 
      start = i+1;
      //Serial.println("Found Comma!");
      //c1 = i;
      /*if(c1 == NULL) {
        c1 = i;
      } else {
         c2 = i;
      }*/
    } 
  }
          Serial.println(); 
  Serial.println(message[strLength]);
  //Serial.println(c1);
  //Serial.println(c2);
}

String extTemp() {
  String temp;
   //sensor_reading = analogRead(sensor_pin);         // stores the digitized (0 - 1023) analog reading from the LM34
   fahrenheit = (100.0 * analogRead(temp_pin) * vref)/1023;   // calculates the actual fahrenheit temperature
   centigrade = (((5.0/9.0))*(fahrenheit-32.0)); //conversion to degrees C
   temp += centigrade; temp += ',';
   temp += fahrenheit; temp += ',';
   if(debug) {
     Serial.print (centigrade); Serial.print("C "); 
     Serial.print(fahrenheit); Serial.print("F ");
   }
   return temp;
}

String intTemp() {
  String temp;
  temp += chipTemp.celsius(); temp += ',';
  temp += chipTemp.fahrenheit(); temp += ',';
  if(debug) {
    Serial.print (chipTemp.celsius()); Serial.print("C "); 
    Serial.print(chipTemp.fahrenheit()); Serial.println("F "); 
  }
  return temp;
}
